# Fritzing sketch rc car (saved by Fritzing 0.9.3b)
breadboards: 1

parts:
  Part1 = Arduino Uno (Rev3)
  S1 = H-Bridge with L298N
  VCC1 = Battery
  M1 = DC Motor
  M2 = DC Motor
  Part2 = Bluetooth HC-05 Macho
  hc-sr1 = hc-sr04

nets:
  N1: Part1.D9_PWM, S1.IN4
  N2: Part1.D10_PWM/SS, Part2.TXD
  N3: Part1.D11_PWM/MOSI, Part2.RXD
  N4: Part1.D12/MISO, hc-sr1.Echo
  N5: Part1.D13/SCK, hc-sr1.Trig
  GND: Part1.GND, VCC1.-, Part2.GND, hc-sr1.GND
  N6: Part1.D3_PWM, S1.IN1
  N7: Part1.D5_PWM, S1.IN2
  N8: Part1.D6_PWM, S1.IN3
  VCC: Part1.5V, Part2.VCC, hc-sr1.VCC
  VIN: Part1.VIN, S1.5V
  N9: S1.12V, VCC1.+
  N10: S1.OUT3-Motor2, M1.pin_2
  N11: S1.OUT4-Motor2, M1.pin_1
  N12: S1.OUT1-Motor1, M2.pin_1
  N13: S1.OUT2-Motor1, M2.pin_2

custom parts:
  H-Bridge with L298N: h-bridge
